# Fritzing sketch Circutree fritz (saved by Fritzing 1.0.4)
breadboards: 1

parts:
  Part1 = Adafruit AS7341
  Part2 = Adafruit LC709203F Fuel Gauge and Battery Monitor [part_number="Adafruit #4712"]
  Part3 = Adafruit PA1010D Mini GPS Module [part_number="Adafruit #4415"]
  A1 = Particle - Photon2
  D1 = SOLAR-IXYS [package=solarbit-12x1]
  Part5 = Adafruit USB LiIon/LiPoly Charger [part_number="Adafruit #259"]
  U1 = LIPO-2000mAh [package=lipo-2000]
  D2 = SOLAR-IXYS [package=solarbit-12x1]
  D3 = SOLAR-IXYS [package=solarbit-12x1]
  Part4 = Adafruit PowerBoost 1000C [part_number="Adafruit #2465"]

nets (from the schematic view):
  GND: Part1.GND, Part2.GND, A1.Pin_4, A1.Pin_30, Part5.GND, D3.A, Part4.GND
  N1: Part1.SDA, Part3.VCC
  N2: Part1.SCL, Part2.SCL, Part3.SCL, A1.Pin_18
  N3: Part2.SDA, Part2.VCC, Part3.SDA, A1.Pin_2, A1.Pin_17, A1.Pin_31
  N4: Part2.VBAT, Part5.BATT
  N5: A1.Pin_28, A1.Pin_29, Part4.VBAT
  N6: D1.C, Part5.5.0V, U1.+, D2.C, D3.C

custom parts:
  Adafruit LC709203F Fuel Gauge and Battery Monitor: Low cost Lithium Polymer batteries have revolutionized electronics - they're thin, they're light, they can be regulated down to 3.3V and they're easy to charge. On your phone, there's a little image of a battery cell that tells you the percentage of charge - so you know when you absolutely need to plug it in and when you can stay untethered. The Adafruit LC709203F LiPoly / LiIon Fuel Gauge and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
  Adafruit PA1010D Mini GPS Module: This miniature GPS breakout is only 1" x 1" (~ 25mm x 25mm) but houses a complete GPS/GNSS solution with both I2C and UART interfaces. There's even an antenna on top so it's plug and play! Support for GPS, GLONASS, GALILEO, QZSS -165 dBm sensitivity, up to 10 Hz updates Up to 210 PRN channels with 99 search channels and 33 simultaneous tracking channels 5V friendly design and only 30mA current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
  Particle - Photon2: The Photon 2 is a microcontroller and Wi-Fi networking developed by particle. Features: 802.11a/b/g/n Wi-Fi, 2.4 GHz and 5 GHz Integrated PCB antenna Integrated U.FL connector for external antenna Integrated RF switch BLE 5 using same antenna as Wi-Fi Realtek RTL8721DM MCU ARM Cortex M33 CPU, 200 MHz 2048 KB (2 MB) user application maximum size 3072 KB (3 MB) of RAM available to user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
  Adafruit USB LiIon/LiPoly Charger: This is a Lithium Ion and Lithium Polymer battery charger based on the MCP73833. It uses a USB mini-B for connection to any computer or 'USB wall adapter'. Charging is performed in three stages: first a preconditioning charge, then a constant-current fast charge and finally a constant-voltage trickle charge to keep the battery topped-up. The fast-charge current is 500mA by default, but is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
  Adafruit PowerBoost 1000C: PowerBoost 1000C is the perfect power supply for your portable project! With a built-in load-sharing battery charger circuit, you'll be able to keep your power-hungry project running even while recharging the battery! This little DC/DC boost converter module can be powered by any 3.7V LiIon/LiPoly battery, and convert the battery output to 5.2V DC for running your 5V projects.
